# Fritzing sketch Hochbeet (saved by Fritzing 0.9.3b)
breadboards: 3

parts:
  Bauteil1 = Adafruit Feather M0 RFM9x LoRa [part_number="Adafruit #3178 or #3179"]
  Bauteil2 = BME280 Breakout
  Bauteil3 = Logic Level Converter
  SONAR1 = Maxbotix MaxSonar Ultrasonic Sensor
  M1 = RioRand LM2596
  Part1 = KY-019 5V Relay Module [package="Breakout board"]
  Bauteil4 = OLED Monochrome 128x64 0.96 inch [part_number=326]
  Bauteil7 = Soil Moisture Sensor
  Bauteil9 = Adafruit Push Button Powerswitch [part_number="Adafruit #1400"]
  Bauteil10 = Adafruit Push Button Powerswitch [part_number="Adafruit #1400"]
  R1 = Resistor [tolerance=±5% resistance=100k package="1206 [SMD]"]
  R2 = Resistor [tolerance=±5% resistance=100k package="1206 [SMD]"]
  Bauteil11 = Adafruit ADS1115 16Bit I2C ADC [part_number="Adafruit #1085"]

nets:
  N1: Bauteil1.A5, Part1.S
  GND: Bauteil1.GND, Bauteil2.GND, Bauteil3.GND, SONAR1.GND, Part1.-, R1.Pin_1, R2.Pin_1
  +3V3: Bauteil1.+3V3, Bauteil2.3.3V, Bauteil3.LV, Part1.+, Bauteil9.IN, Bauteil10.IN
  N2: Bauteil1.D13, Bauteil9.OUT, R2.Pin_0
  N3: Bauteil1.D12, Bauteil10.OUT, R1.Pin_0
  N4: Bauteil1.SCL, Bauteil2.SCK/SCL, Bauteil3.TX2_LV, Bauteil4.RESET
  N5: Bauteil1.SDA, Bauteil2.SDI/SDA, Bauteil3.TX_LV, Bauteil4.CS
  N6: Bauteil3.TX_HV, SONAR1.RX, Bauteil11.SDA
  N7: Bauteil3.TX2_HV, SONAR1.TX, Bauteil11.SCL
  N8: SONAR1.AN, M1.Pin_3
  N9: Bauteil7.SIG, Bauteil11.AIN0
  GND_2: Bauteil7.GND, Bauteil11.GND
  VCC: Bauteil7.VCC, Bauteil11.VDD

notes:
  12V von Solar
  5V
  Wasserlevel sensoren
  Tensiometer
  Flower Pot Full
  Water Tank Empty

custom parts:
  Adafruit Feather M0 RFM9x LoRa: This is the Adafruit Feather M0 RFM95 LoRa Radio - our take on an microcontroller with a "Long Range (LoRa)" packet radio transceiver with built in USB and battery charging. Its an Adafruit Feather M0 with a 433Mhz or 900MHz radio module cooked in! Great for making wireless networks that are more flexible than Bluetooth LE and without the high power requirements of WiFi. We have other boards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
  Maxbotix MaxSonar Ultrasonic Sensor: Maxbotix MaxSonar Ultrasonic Sensor LV-EZ0, LV-EZ1, LV-EZ2, LV-EZ3, LV-EZ4
  KY-019 5V Relay Module: KY-019 5V Relay module, used to control AC circuits.
  OLED Monochrome 128x64 0.96 inch: These displays are small, only about 1" diameter, but very readable due to the high contrast of an OLED display. This display is made of 128x64 individual white OLED pixels, each one is turned on or off by the controller chip. Because the display makes its own light, no backlight is required. This reduces the power required to run the OLED and is why the display has such high contrast; we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
  Adafruit Push Button Powerswitch: The Adafruit Push-button Power Switch is a tidy little design that lets you control a DC power source using an everyday tactile button. The breakout uses a latching analog circuit that is triggered by a push of the button. Press once to turn on, then press again to turn off. The circuit uses a 3A P-FET to connect and disconnect the IN pin to the OUT pin. Works great from 3V to 14VDC and up to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
  Adafruit ADS1115 16Bit I2C ADC: For microcontrollers without an analog-to-digital converter or when you want a higher-precision ADC, the ADS1115 provides 16-bit precision at 860 samples/second over I2C. The chip can be configured as 4 single-ended input channels, or two differential channels. As a nice bonus, it even includes a programmable gain amplifier, up to x16, to help boost up smaller single/differential signals to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
